# Fritzing sketch potentiometre 10k (saved by Fritzing 0.9.3b)
breadboards: 1

parts:
  Composant1 = Arduino Uno (Rev3)
  LED1 = LED - 5mm [color="Red (633nm)" package="5 mm [THT]"]
  R1 = Trimmer Potentiometer [maximum_resistance=10kΩ package=THT]

nets:
  N1: Composant1.5V, LED1.anode, R1.leg2
  N2: Composant1.GND, LED1.cathode
